// Digital circuit alu.dig as structural Verilog
module alu (
  input  [7:0] a,
  input  [7:0] b,
  input  [3:0] alu_op,
  output [7:0] result,
  output zero,
  output carry,
  output negative,
  output overflow
);

  wire add_1_c_o, and_2_out, and_3_out, comparator_1_eq, sub_1_c_o, xnor_1_out, xor_2_out, xor_3_out;
  wire [7:0] add_1_s, and_1_out, or_1_out, sub_1_s, xor_1_out;

  Comparator #(.Bits(4)) comparator_1 (.a(alu_op), .b(4'b0010), .eq(comparator_1_eq));  // open: gt, lt
  Add #(.Bits(8)) add_1 (.a(a), .b(b), .c_i(1'b0), .s(add_1_s), .c_o(add_1_c_o));
  Sub #(.Bits(8)) sub_1 (.a(a), .b(b), .c_i(1'b0), .s(sub_1_s), .c_o(sub_1_c_o));
  assign and_1_out = a & b;  // And and_1, 8 bits wide
  assign or_1_out = a | b;  // Or or_1, 8 bits wide
  assign xor_1_out = a ^ b;  // XOr xor_1, 8 bits wide
  Multiplexer #(.Bits(8), .Selector_Bits(4)) multiplexer_1 (
    .sel(alu_op), .in_0({8{1'b0}}), .in_1(add_1_s), .in_2(sub_1_s), .in_3(and_1_out), .in_4(or_1_out),
    .in_5(xor_1_out), .in_6({8{1'b0}}), .in_7({8{1'b0}}), .in_8(b), .in_9(add_1_s), .in_10({8{1'b0}}),
    .in_11({8{1'b0}}), .in_12({8{1'b0}}), .in_13({8{1'b0}}), .in_14({8{1'b0}}), .in_15({8{1'b0}}),
    .out({negative, result[6:0]}));
  Multiplexer multiplexer_2 (.sel(comparator_1_eq), .in_0(add_1_c_o), .in_1(sub_1_c_o), .out(carry));
  Comparator #(.Bits(8)) comparator_2 (.a({negative, result[6:0]}), .b({8{1'b0}}), .eq(zero));  // open: gt, lt
  xnor xnor_1 (xnor_1_out, a[7], b[7]);
  xor xor_2 (xor_2_out, a[7], negative);
  xor xor_3 (xor_3_out, a[7], b[7]);
  and and_2 (and_2_out, xnor_1_out, xor_2_out);
  and and_3 (and_3_out, xor_2_out, xor_3_out);
  Multiplexer multiplexer_3 (.sel(comparator_1_eq), .in_0(and_2_out), .in_1(and_3_out), .out(overflow));

  assign result[7] = negative;
endmodule
