// Digital circuit control_unit.dig as structural Verilog
module control_unit (
  input  clk,
  input  reset,
  input  [3:0] opcode,
  input  zero_flag,
  input  negative_flag,
  input  overflow_flag,
  output pc_enable,
  output pc_load,
  output ir_load,
  output reg_write,
  output [3:0] alu_op,
  output alu_src,
  output mem_read,
  output mem_write
);

  wire ADD_2_eq, ADDI_eq, and_2_out, and_3_out, and_4_out, and_5_out, and_6_out, and_7_out, and_8_out,
       and_10_out, and_12_out, and_13_out, and_14_out, AND_eq, BEQ_eq, BLT_eq, BNE_eq, DECODER_eq,
       EXECUTE_eq, JMP_eq, LOAD_eq, MOV_eq, not_1_out, or_2_out, or_3_out, or_4_out, or_5_out, OR_eq,
       STORE_eq, SUB_eq, WRITEBACK_eq, xor_2_out, XOR_eq;
  wire [1:0] add_1_s, multiplexer_1_out, register_1_q;
  wire [3:0] multiplexer_2_out, multiplexer_3_out, multiplexer_4_out, multiplexer_5_out;

  Multiplexer #(.Bits(2)) multiplexer_1 (.sel(reset), .in_0(add_1_s), .in_1(2'b00), .out(multiplexer_1_out));
  Register #(.Bits(2)) register_1 (.D(multiplexer_1_out), .C(clk), .en(1'b1), .Q(register_1_q));
  Add #(.Bits(2)) add_1 (.a(register_1_q), .b(2'b01), .c_i(1'b0), .s(add_1_s));  // open: c_o
  Comparator #(.Bits(2)) FETCH (.a(register_1_q), .b(2'b00), .eq(ir_load));  // open: gt, lt
  Comparator #(.Bits(2)) DECODER (.a(register_1_q), .b(2'b01), .eq(DECODER_eq));  // open: gt, lt
  Comparator #(.Bits(2)) EXECUTE (.a(register_1_q), .b(2'b10), .eq(EXECUTE_eq));  // open: gt, lt
  Comparator #(.Bits(2)) WRITEBACK (.a(register_1_q), .b(2'b11), .eq(WRITEBACK_eq));  // open: gt, lt
  Comparator #(.Bits(4)) ADD_2 (.a(opcode), .b(4'b0001), .eq(ADD_2_eq));  // open: gt, lt
  Comparator #(.Bits(4)) SUB (.a(opcode), .b(4'b0010), .eq(SUB_eq));  // open: gt, lt
  Comparator #(.Bits(4)) AND (.a(opcode), .b(4'b0011), .eq(AND_eq));  // open: gt, lt
  Comparator #(.Bits(4)) OR (.a(opcode), .b(4'b0100), .eq(OR_eq));  // open: gt, lt
  Comparator #(.Bits(4)) XOR (.a(opcode), .b(4'b0101), .eq(XOR_eq));  // open: gt, lt
  Comparator #(.Bits(4)) LOAD (.a(opcode), .b(4'b0110), .eq(LOAD_eq));  // open: gt, lt
  Comparator #(.Bits(4)) STORE (.a(opcode), .b(4'b0111), .eq(STORE_eq));  // open: gt, lt
  Comparator #(.Bits(4)) MOV (.a(opcode), .b(4'b1000), .eq(MOV_eq));  // open: gt, lt
  Comparator #(.Bits(4)) ADDI (.a(opcode), .b(4'b1001), .eq(ADDI_eq));  // open: gt, lt
  Comparator #(.Bits(4)) JMP (.a(opcode), .b(4'b1010), .eq(JMP_eq));  // open: gt, lt
  Comparator #(.Bits(4)) BEQ (.a(opcode), .b(4'b1011), .eq(BEQ_eq));  // open: gt, lt
  Comparator #(.Bits(4)) BNE (.a(opcode), .b(4'b1100), .eq(BNE_eq));  // open: gt, lt
  Comparator #(.Bits(4)) BLT (.a(opcode), .b(4'b1101), .eq(BLT_eq));  // open: gt, lt
  and and_2 (and_2_out, LOAD_eq, EXECUTE_eq);
  and and_3 (and_3_out, LOAD_eq, WRITEBACK_eq);
  or or_2 (or_2_out, ADD_2_eq, SUB_eq, AND_eq, OR_eq, XOR_eq, ADDI_eq, MOV_eq, LOAD_eq);
  and and_4 (and_4_out, ADDI_eq, EXECUTE_eq);
  and and_5 (and_5_out, ADDI_eq, WRITEBACK_eq);
  and and_6 (and_6_out, WRITEBACK_eq, JMP_eq);
  and and_7 (and_7_out, BNE_eq, WRITEBACK_eq);
  xor xor_2 (xor_2_out, negative_flag, overflow_flag);
  and and_8 (and_8_out, BLT_eq, WRITEBACK_eq);
  and and_9 (mem_write, STORE_eq, WRITEBACK_eq);
  not not_1 (not_1_out, zero_flag);
  and and_10 (and_10_out, BEQ_eq, WRITEBACK_eq);
  or or_3 (or_3_out, BLT_eq, BEQ_eq, BNE_eq);
  or or_4 (or_4_out, XOR_eq, OR_eq, AND_eq, SUB_eq, ADD_2_eq);
  or or_5 (or_5_out, WRITEBACK_eq, EXECUTE_eq);
  or or_6 (mem_read, and_2_out, and_3_out);
  and and_11 (reg_write, WRITEBACK_eq, or_2_out);
  or or_7 (alu_src, and_4_out, and_5_out);
  and and_12 (and_12_out, and_7_out, not_1_out);
  and and_13 (and_13_out, xor_2_out, and_8_out);
  and and_14 (and_14_out, and_10_out, zero_flag);
  or or_8 (pc_load, and_6_out, and_12_out, and_13_out, and_14_out);
  Multiplexer #(.Bits(4)) multiplexer_2 (.sel(or_4_out), .in_0(4'b0000), .in_1(opcode), .out(multiplexer_2_out));
  Multiplexer #(.Bits(4)) multiplexer_3 (
    .sel(MOV_eq), .in_0(multiplexer_2_out), .in_1(4'b1000), .out(multiplexer_3_out));
  Multiplexer #(.Bits(4)) multiplexer_4 (
    .sel(ADDI_eq), .in_0(multiplexer_3_out), .in_1(4'b1001), .out(multiplexer_4_out));
  Multiplexer #(.Bits(4)) multiplexer_5 (
    .sel(or_3_out), .in_0(multiplexer_4_out), .in_1(4'b0010), .out(multiplexer_5_out));
  Multiplexer #(.Bits(4)) multiplexer_6 (.sel(or_5_out), .in_0(4'b0000), .in_1(multiplexer_5_out), .out(alu_op));

  assign pc_enable = ir_load;
endmodule
