// Digital circuit cpu_core_test.dig as structural Verilog
module cpu_core_test (
  input  clk,
  input  reset
);

  wire alu_1_negative, alu_1_overflow, alu_1_zero, comparator_1_eq, control_unit_1_alu_src,
       control_unit_1_ir_load, control_unit_1_mem_read, control_unit_1_mem_write, control_unit_1_pc_enable,
       control_unit_1_pc_load, control_unit_1_reg_write;
  wire [2:0] decoder_1_rd, decoder_1_rs;
  wire [3:0] control_unit_1_alu_op, decoder_1_opcode;
  wire [7:0] alu_1_result, bitextender_1_out, data_memory_1_read_data, multiplexer_1_out, multiplexer_2_out,
       program_counter_1_pc_out, reg_file_1_read_data1, reg_file_1_read_data2;
  wire [7:2] decoder_1_imm6;
  wire [15:0] add_1_s, bitextender_2_out, instruction_memory_1_instruction,
       instruction_register_1_instruction_out, multiplexer_3_out;
  wire [15:8] program_counter_1_pc_out_2;

  reg_file reg_file_1 (
    .clk(clk), .reg_write(control_unit_1_reg_write), .read_reg1(decoder_1_rd), .read_reg2(decoder_1_rs),
    .write_reg(decoder_1_rd), .write_data(multiplexer_2_out), .read_data1(reg_file_1_read_data1),
    .read_data2(reg_file_1_read_data2));
  program_counter program_counter_1 (
    .clk(clk), .reset(reset), .pc_load(control_unit_1_pc_load), .pc_in(multiplexer_3_out),
    .pc_enable(control_unit_1_pc_enable), .pc_out({program_counter_1_pc_out_2, program_counter_1_pc_out}));
  control_unit control_unit_1 (
    .clk(clk), .reset(reset), .opcode(decoder_1_opcode), .zero_flag(alu_1_zero),
    .negative_flag(alu_1_negative), .overflow_flag(alu_1_overflow), .pc_enable(control_unit_1_pc_enable),
    .pc_load(control_unit_1_pc_load), .ir_load(control_unit_1_ir_load), .reg_write(control_unit_1_reg_write),
    .alu_op(control_unit_1_alu_op), .alu_src(control_unit_1_alu_src), .mem_read(control_unit_1_mem_read),
    .mem_write(control_unit_1_mem_write));
  data_memory data_memory_1 (
    .clk(clk), .mem_read(control_unit_1_mem_read), .mem_write(control_unit_1_mem_write),
    .address({decoder_1_imm6, 2'b00}), .write_data(reg_file_1_read_data2), .read_data(data_memory_1_read_data));
  instruction_register instruction_register_1 (
    .instruction_in(instruction_memory_1_instruction), .clk(clk), .reset(reset),
    .ir_load(control_unit_1_ir_load), .instruction_out(instruction_register_1_instruction_out));
  // Probe on {program_counter_1_pc_out_2, program_counter_1_pc_out}
  // Probe on control_unit_1_alu_op
  // Probe on alu_1_zero
  alu alu_1 (
    .a(reg_file_1_read_data1), .b(multiplexer_1_out), .alu_op(control_unit_1_alu_op), .result(alu_1_result),
    .zero(alu_1_zero), .negative(alu_1_negative), .overflow(alu_1_overflow));  // open: carry
  decoder decoder_1 (
    .instruction_in(instruction_register_1_instruction_out), .imm6(decoder_1_imm6), .rs(decoder_1_rs),
    .rd(decoder_1_rd), .opcode(decoder_1_opcode));
  instruction_memory instruction_memory_1 (
    .address(program_counter_1_pc_out), .instruction(instruction_memory_1_instruction));
  // Probe on alu_1_result
  BitExtender #(.inputBits(6), .outputBits(8)) bitextender_1 (.in(decoder_1_imm6), .out(bitextender_1_out));
  Multiplexer #(.Bits(8)) multiplexer_1 (
    .sel(control_unit_1_alu_src), .in_0(reg_file_1_read_data2), .in_1(bitextender_1_out),
    .out(multiplexer_1_out));
  Multiplexer #(.Bits(8)) multiplexer_2 (
    .sel(control_unit_1_mem_read), .in_0(alu_1_result), .in_1(data_memory_1_read_data),
    .out(multiplexer_2_out));
  Multiplexer #(.Bits(16)) multiplexer_3 (
    .sel(comparator_1_eq), .in_0(add_1_s), .in_1({{10{1'b0}}, decoder_1_imm6}), .out(multiplexer_3_out));
  Add #(.Bits(16)) add_1 (
    .a({program_counter_1_pc_out_2, program_counter_1_pc_out}), .b(bitextender_2_out), .c_i(1'b0), .s(add_1_s));  // open: c_o
  BitExtender #(.inputBits(6)) bitextender_2 (.in(decoder_1_imm6), .out(bitextender_2_out));
  Comparator #(.Bits(4)) comparator_1 (.a(decoder_1_opcode), .b(4'b1010), .eq(comparator_1_eq));  // open: gt, lt

  // Notes on the sheet:
  //   clk: Hz: 10
endmodule
