// Digital circuit data_memory.dig as structural Verilog
module data_memory (
  input  clk,
  input  mem_read,
  input  mem_write,
  input  [7:0] address,
  input  [7:0] write_data,
  output [7:0] read_data
);

  RAMDualPort #(.AddrBits(8), .Bits(8)) ramdualport_1 (
    .A(address), .Din(write_data), .str(mem_write), .C(clk), .ld(mem_read), .D(read_data));
endmodule
