// Digital circuit instruction_memory.dig as structural Verilog
module instruction_memory (
  input  [7:0] address,
  output [15:0] instruction
);

  ROM #(.AddrBits(8), .Bits(16)) rom_1 (.A(address), .sel(1'b1), .D(instruction));

  // Notes on the sheet:
  //   contents of rom_1 (hex, n*v repeats v):
  //   9205,9405,b281,9601,9809,780a,6a0a,9c05,9c3f,dc01,b03d,a00b
endmodule
