// Digital circuit instruction_register.dig as structural Verilog
module instruction_register (
  input  [15:0] instruction_in,
  input  clk,
  input  reset,
  input  ir_load,
  output [15:0] instruction_out
);

  wire or_1_out;
  wire [15:0] multiplexer_1_out;

  Multiplexer #(.Bits(16)) multiplexer_1 (
    .sel(reset), .in_0(instruction_in), .in_1({16{1'b0}}), .out(multiplexer_1_out));
  or or_1 (or_1_out, reset, ir_load);
  Register #(.Bits(16)) register_1 (.D(multiplexer_1_out), .C(clk), .en(or_1_out), .Q(instruction_out));
endmodule
