// Digital circuit program_counter.dig as structural Verilog
module program_counter (
  input  clk,
  input  reset,
  input  pc_load,
  input  [15:0] pc_in,
  input  pc_enable,
  output [15:0] pc_out
);

  wire [15:0] add_1_s, multiplexer_1_out, multiplexer_2_out, multiplexer_3_out;

  Add #(.Bits(16)) add_1 (.a(pc_out), .b(16'h1), .c_i(1'b0), .s(add_1_s));  // open: c_o
  Multiplexer #(.Bits(16)) multiplexer_1 (.sel(pc_enable), .in_0(pc_out), .in_1(add_1_s), .out(multiplexer_1_out));
  Multiplexer #(.Bits(16)) multiplexer_2 (
    .sel(pc_load), .in_0(multiplexer_1_out), .in_1(pc_in), .out(multiplexer_2_out));
  Multiplexer #(.Bits(16)) multiplexer_3 (
    .sel(reset), .in_0(multiplexer_2_out), .in_1({16{1'b0}}), .out(multiplexer_3_out));
  Register #(.Bits(16)) register_1 (.D(multiplexer_3_out), .C(clk), .en(1'b1), .Q(pc_out));
endmodule
