// Digital circuit reg_file.dig as structural Verilog
module reg_file (
  input  clk,
  input  reg_write,
  input  [2:0] read_reg1,
  input  [2:0] read_reg2,
  input  [2:0] write_reg,
  input  [7:0] write_data,
  output [7:0] read_data1,
  output [7:0] read_data2
);

  wire and_1_out, and_2_out, and_3_out, and_4_out, and_5_out, and_6_out, and_7_out, decoder_1_out_1,
       decoder_1_out_2, decoder_1_out_3, decoder_1_out_4, decoder_1_out_5, decoder_1_out_6, decoder_1_out_7;
  wire [7:0] R1_q, R2_q, R3_q, R4_q, R5_q, R6_q, R7_q;

  Decoder #(.Selector_Bits(3)) decoder_1 (
    .sel(write_reg), .out_1(decoder_1_out_1), .out_2(decoder_1_out_2), .out_3(decoder_1_out_3),
    .out_4(decoder_1_out_4), .out_5(decoder_1_out_5), .out_6(decoder_1_out_6), .out_7(decoder_1_out_7));  // open: out_0
  and and_1 (and_1_out, decoder_1_out_1, reg_write);
  and and_2 (and_2_out, decoder_1_out_2, reg_write);
  and and_3 (and_3_out, decoder_1_out_3, reg_write);
  and and_4 (and_4_out, decoder_1_out_4, reg_write);
  and and_5 (and_5_out, decoder_1_out_5, reg_write);
  and and_6 (and_6_out, decoder_1_out_6, reg_write);
  and and_7 (and_7_out, decoder_1_out_7, reg_write);
  Register #(.Bits(8)) R0 (.D(write_data), .C(clk), .en(1'b0));  // open: Q
  Register #(.Bits(8)) R1 (.D(write_data), .C(clk), .en(and_1_out), .Q(R1_q));
  Register #(.Bits(8)) R2 (.D(write_data), .C(clk), .en(and_2_out), .Q(R2_q));
  Register #(.Bits(8)) R3 (.D(write_data), .C(clk), .en(and_3_out), .Q(R3_q));
  Register #(.Bits(8)) R4 (.D(write_data), .C(clk), .en(and_4_out), .Q(R4_q));
  Register #(.Bits(8)) R5 (.D(write_data), .C(clk), .en(and_5_out), .Q(R5_q));
  Register #(.Bits(8)) R6 (.D(write_data), .C(clk), .en(and_6_out), .Q(R6_q));
  Register #(.Bits(8)) R7 (.D(write_data), .C(clk), .en(and_7_out), .Q(R7_q));
  Multiplexer #(.Bits(8), .Selector_Bits(3)) multiplexer_1 (
    .sel(read_reg1), .in_0({8{1'b0}}), .in_1(R1_q), .in_2(R2_q), .in_3(R3_q), .in_4(R4_q), .in_5(R5_q),
    .in_6(R6_q), .in_7(R7_q), .out(read_data1));
  Multiplexer #(.Bits(8), .Selector_Bits(3)) multiplexer_2 (
    .sel(read_reg2), .in_0({8{1'b0}}), .in_1(R1_q), .in_2(R2_q), .in_3(R3_q), .in_4(R4_q), .in_5(R5_q),
    .in_6(R6_q), .in_7(R7_q), .out(read_data2));
endmodule
