// Logisim project alu.circ as structural Verilog: 1 circuit, main circuit alu
module alu (
  input  [7:0] A,
  input  [7:0] B,
  input  [3:0] alu_op,
  output [7:0] result,
  output zero,
  output negative,
  output carry,
  output overflow
);

  wire adder_1_cout, adder_2_cout, and_2_out, and_3_out, comparator_2_eq, comparator_3_eq, comparator_4_eq,
       comparator_6_eq, xnor_1_out, xor_2_out, xor_3_out;
  wire [1:0] or_2_out;
  wire [7:0] and_1_out, not_1_out, or_1_out, xor_1_out;
  wire [8:0] adder_1_out, adder_2_out, bit_extender_1_out, bit_extender_2_out, bit_extender_3_out;

  assign not_1_out = ~B;  // NOT_Gate not_1, 8 bits wide
  assign and_1_out = A & B;  // AND_Gate and_1, 8 bits wide
  assign or_1_out = A | B;  // OR_Gate or_1, 8 bits wide
  assign xor_1_out = A ^ B;  // XOR_Gate xor_1, 8 bits wide
  assign bit_extender_1_out = {{1{1'b0}}, A};  // Bit_Extender bit_extender_1
  assign bit_extender_2_out = {{1{1'b0}}, B};  // Bit_Extender bit_extender_2
  assign bit_extender_3_out = {{1{1'b0}}, not_1_out};  // Bit_Extender bit_extender_3
  Adder #(.width(9)) adder_1 (
    .a(bit_extender_1_out), .b(bit_extender_2_out), .out(adder_1_out), .cout(adder_1_cout));  // open: cin
  Adder #(.width(9)) adder_2 (
    .a(bit_extender_1_out), .b(bit_extender_3_out), .out(adder_2_out), .cin(1'b1), .cout(adder_2_cout));
  Comparator #(.width(4)) comparator_1 (.a(alu_op), .b(4'b0001));  // open: gt, eq, lt
  Comparator #(.width(4)) comparator_2 (.a(alu_op), .b(4'b0010), .eq(comparator_2_eq));  // open: gt, lt
  Comparator #(.width(4)) comparator_3 (.a(alu_op), .b(4'b0011), .eq(comparator_3_eq));  // open: gt, lt
  Comparator #(.width(4)) comparator_4 (.a(alu_op), .b(4'b0100), .eq(comparator_4_eq));  // open: gt, lt
  Multiplexer #(.select(4), .width(8)) multiplexer_1 (
    .in0({8{1'b0}}), .in1(adder_1_out[7:0]), .in2(adder_2_out[7:0]), .in3(and_1_out), .in4(or_1_out),
    .in5(xor_1_out), .in6({8{1'b0}}), .in7({8{1'b0}}), .in8(A), .in9(adder_1_out[7:0]), .in10({8{1'b0}}),
    .in11(adder_2_out[7:0]), .in12(adder_2_out[7:0]), .in13({A[6:0], 1'b0}), .in14({1'b0, A[7:1]}),
    .out({negative, result[6:0]}), .sel(alu_op));  // open: in15
  or or_2 (or_2_out[0], comparator_2_eq, comparator_4_eq);
  or or_3 (or_2_out[1], comparator_3_eq, comparator_4_eq);
  xnor xnor_1 (xnor_1_out, A[7], B[7]);
  xor xor_2 (xor_2_out, A[7], negative);
  xor xor_3 (xor_3_out, A[7], B[7]);
  Multiplexer #(.select(2)) multiplexer_2 (
    .in0(adder_1_cout), .in1(adder_2_cout), .in2(A[7]), .in3(A[0]), .out(carry), .sel(or_2_out));
  and and_2 (and_2_out, xnor_1_out, xor_2_out);
  and and_3 (and_3_out, xor_2_out, xor_3_out);
  Comparator comparator_5 (.a({negative, result[6:0]}), .b({8{1'b0}}), .eq(zero));  // open: gt, lt
  Multiplexer multiplexer_3 (.in0(and_2_out), .in1(and_3_out), .out(overflow), .sel(comparator_6_eq));
  Comparator #(.width(4)) comparator_6 (.a(4'b0010), .b(alu_op), .eq(comparator_6_eq));  // open: gt, lt

  assign result[7] = negative;
endmodule
