// Logisim project control_unit.circ as structural Verilog: 1 circuit, main circuit control_unit
module control_unit (
  input  clk,
  input  reset,
  input  [3:0] opcode,
  input  zero,
  input  negative,
  input  overflow,
  output pc_enable,
  output ir_load,
  output mem_read,
  output mem_write,
  output alu_src,
  output pc_load,
  output reg_write,
  output [3:0] alu_op
);

  wire and_5_out, and_6_out, and_7_out, and_8_out, and_9_out, BEQ, BLT, BNE, comparator_5_eq,
       comparator_6_eq, comparator_7_eq, comparator_8_eq, comparator_9_eq, comparator_10_eq,
       comparator_11_eq, comparator_12_eq, comparator_13_eq, comparator_14_eq, comparator_19_eq,
       comparator_20_eq, exec, JMP, not_1_out, or_1_out, or_2_out, or_3_out, or_4_out, or_5_out, wb,
       xor_1_out;
  wire [1:0] adder_1_out, multiplexer_1_out, register_1_q;
  wire [3:0] multiplexer_2_out;

  Register #(.width(2)) register_1 (.D(multiplexer_1_out), .clk(clk), .Q(register_1_q));  // open: en, clr
  Adder #(.width(2)) adder_1 (.a(register_1_q), .b(2'b01), .out(adder_1_out));  // open: cin, cout
  Multiplexer #(.width(2)) multiplexer_1 (.in0(adder_1_out), .in1(2'b00), .out(multiplexer_1_out), .sel(reset));
  Comparator #(.width(2)) comparator_1 (.a(register_1_q), .b(2'b00), .eq(ir_load));  // open: gt, lt
  Comparator #(.width(2)) comparator_2 (.a(register_1_q), .b(2'b01));  // open: gt, eq, lt
  Comparator #(.width(2)) comparator_3 (.a(register_1_q), .b(2'b10), .eq(exec));  // open: gt, lt
  Comparator #(.width(2)) comparator_4 (.a(register_1_q), .b(2'b11), .eq(wb));  // open: gt, lt
  Comparator #(.width(4)) comparator_5 (.a(opcode), .b(4'b0000), .eq(comparator_5_eq));  // open: gt, lt
  Comparator #(.width(4)) comparator_6 (.a(opcode), .b(4'b0001), .eq(comparator_6_eq));  // open: gt, lt
  Comparator #(.width(4)) comparator_7 (.a(opcode), .b(4'b0010), .eq(comparator_7_eq));  // open: gt, lt
  Comparator #(.width(4)) comparator_8 (.a(opcode), .b(4'b0011), .eq(comparator_8_eq));  // open: gt, lt
  Comparator #(.width(4)) comparator_9 (.a(opcode), .b(4'b0100), .eq(comparator_9_eq));  // open: gt, lt
  Comparator #(.width(4)) comparator_10 (.a(opcode), .b(4'b0101), .eq(comparator_10_eq));  // open: gt, lt
  Comparator #(.width(4)) comparator_11 (.a(opcode), .b(4'b0110), .eq(comparator_11_eq));  // open: gt, lt
  Comparator #(.width(4)) comparator_12 (.a(opcode), .b(4'b0111), .eq(comparator_12_eq));  // open: gt, lt
  Comparator #(.width(4)) comparator_13 (.a(opcode), .b(4'b1000), .eq(comparator_13_eq));  // open: gt, lt
  Comparator #(.width(4)) comparator_14 (.a(opcode), .b(4'b1001), .eq(comparator_14_eq));  // open: gt, lt
  Comparator #(.width(4)) comparator_15 (.a(opcode), .b(4'b1010), .eq(JMP));  // open: gt, lt
  Comparator #(.width(4)) comparator_16 (.a(opcode), .b(4'b1011), .eq(BEQ));  // open: gt, lt
  Comparator #(.width(4)) comparator_17 (.a(opcode), .b(4'b1100), .eq(BNE));  // open: gt, lt
  Comparator #(.width(4)) comparator_18 (.a(opcode), .b(4'b1101), .eq(BLT));  // open: gt, lt
  Comparator #(.width(4)) comparator_19 (.a(opcode), .b(4'b1110), .eq(comparator_19_eq));  // open: gt, lt
  Comparator #(.width(4)) comparator_20 (.a(opcode), .b(4'b1111), .eq(comparator_20_eq));  // open: gt, lt
  or or_1 (or_1_out, exec, wb);
  and and_1 (mem_write, wb, comparator_12_eq);
  and and_2 (mem_read, comparator_11_eq, or_1_out);
  or or_2 (or_2_out, comparator_6_eq, comparator_7_eq, comparator_8_eq, comparator_9_eq, comparator_10_eq, comparator_13_eq, comparator_14_eq, comparator_11_eq, comparator_19_eq, comparator_20_eq);
  or or_3 (or_3_out, comparator_5_eq, comparator_11_eq, comparator_12_eq, JMP);
  or or_4 (or_4_out, BEQ, BNE, BLT);
  or or_5 (or_5_out, exec, wb);
  and and_3 (reg_write, or_2_out, wb);
  and and_4 (alu_src, or_5_out, comparator_13_eq);
  not not_1 (not_1_out, zero);
  and and_5 (and_5_out, wb, BEQ);
  xor xor_1 (xor_1_out, negative, overflow);
  Multiplexer #(.width(4)) multiplexer_2 (.in0(opcode), .in1(4'b0000), .out(multiplexer_2_out), .sel(or_3_out));
  and and_6 (and_6_out, wb, BNE, not_1_out);
  and and_7 (and_7_out, zero, and_5_out);
  and and_8 (and_8_out, wb, BLT, xor_1_out);
  and and_9 (and_9_out, wb, JMP);
  Multiplexer #(.width(4)) multiplexer_3 (.in0(multiplexer_2_out), .in1(4'b0010), .out(alu_op), .sel(or_4_out));
  or or_6 (pc_load, and_6_out, and_7_out, and_8_out, and_9_out);

  assign pc_enable = ir_load;
endmodule
