// Logisim project cpu_core.circ as structural Verilog: 1 circuit, main circuit main
module main (
  input  reset,
  input  [7:0] manual_data,
  input  [2:0] manual_reg,
  input  manual_enable,
  output [15:0] PC_out,
  output [7:0] ALU_result,
  output [7:0] REG_writeData,
  output [15:0] IR_instOut
);

  wire alu_1_negative, alu_1_overflow, alu_1_zero, clk, comparator_1_eq, control_unit_1_alu_src,
       control_unit_1_ir_load, control_unit_1_mem_read, control_unit_1_mem_write, control_unit_1_pc_enable,
       control_unit_1_pc_load, control_unit_1_reg_write, or_1_out;
  wire [2:0] multiplexer_1_out, rd, rs;
  wire [3:0] control_unit_1_alu_op, decoder_logic_1_opcode;
  wire [5:0] decoder_logic_1_imm6;
  wire [7:0] bit_extender_1_out, bit_extender_3_out, data_memory_1_read_data, multiplexer_2_out,
       multiplexer_3_out, reg_file_1_read_data1, reg_file_1_read_data2;
  wire [15:0] adder_1_out, bit_extender_2_out, bit_extender_4_out, instruction_memory_1_instruction,
       multiplexer_5_out;

  Clock u_clk (.out(clk));
  Multiplexer #(.width(3)) multiplexer_1 (.in0(rd), .in1(manual_reg), .out(multiplexer_1_out), .sel(manual_enable));
  or or_1 (or_1_out, manual_enable, control_unit_1_reg_write);
  Multiplexer #(.width(8)) multiplexer_2 (
    .in0(ALU_result), .in1(data_memory_1_read_data), .out(multiplexer_2_out), .sel(control_unit_1_mem_read));
  alu alu_1 (
    .A(reg_file_1_read_data1), .B(multiplexer_3_out), .alu_op(control_unit_1_alu_op), .result(ALU_result),
    .zero(alu_1_zero), .negative(alu_1_negative), .overflow(alu_1_overflow));  // open: carry
  control_unit control_unit_1 (
    .clk(clk), .reset(reset), .opcode(decoder_logic_1_opcode), .zero(alu_1_zero), .negative(alu_1_negative),
    .overflow(alu_1_overflow), .pc_enable(control_unit_1_pc_enable), .ir_load(control_unit_1_ir_load),
    .mem_read(control_unit_1_mem_read), .mem_write(control_unit_1_mem_write),
    .alu_src(control_unit_1_alu_src), .pc_load(control_unit_1_pc_load), .reg_write(control_unit_1_reg_write),
    .alu_op(control_unit_1_alu_op));
  data_memory data_memory_1 (
    .address(bit_extender_1_out), .mem_write(control_unit_1_mem_write), .mem_read(control_unit_1_mem_read),
    .clk(clk), .write_data(reg_file_1_read_data1), .read_data(data_memory_1_read_data));
  reg_file reg_file_1 (
    .reg_write(or_1_out), .write_reg(multiplexer_1_out), .write_data(REG_writeData), .clk(clk),
    .reset(reset), .read_reg1(rd), .read_reg2(rs), .read_data1(reg_file_1_read_data1),
    .read_data2(reg_file_1_read_data2));
  Multiplexer #(.width(8)) multiplexer_3 (
    .in0(reg_file_1_read_data2), .in1(bit_extender_3_out), .out(multiplexer_3_out),
    .sel(control_unit_1_alu_src));
  Multiplexer #(.width(8)) multiplexer_4 (
    .in0(multiplexer_2_out), .in1(manual_data), .out(REG_writeData), .sel(manual_enable));
  decoder_logic decoder_logic_1 (
    .instruction(IR_instOut), .imm6(decoder_logic_1_imm6), .rs(rs), .rd(rd), .opcode(decoder_logic_1_opcode));
  instruction_memory instruction_memory_1 (.address(PC_out[7:0]), .instruction(instruction_memory_1_instruction));
  instruction_register instruction_register_1 (
    .instruction_in(instruction_memory_1_instruction), .reset(reset), .ir_load(control_unit_1_ir_load),
    .clk(clk), .instruction_out(IR_instOut));
  assign bit_extender_1_out = {{2{1'b0}}, decoder_logic_1_imm6};  // Bit_Extender bit_extender_1
  assign bit_extender_2_out = {{10{decoder_logic_1_imm6[5]}}, decoder_logic_1_imm6};  // Bit_Extender bit_extender_2
  assign bit_extender_3_out = {{2{decoder_logic_1_imm6[5]}}, decoder_logic_1_imm6};  // Bit_Extender bit_extender_3
  assign bit_extender_4_out = {{10{1'b0}}, decoder_logic_1_imm6};  // Bit_Extender bit_extender_4
  program_counter program_counter_1 (
    .clk(clk), .pc_next(multiplexer_5_out), .reset(reset), .pc_load(control_unit_1_pc_load),
    .pc_enable(control_unit_1_pc_enable), .pc_out(PC_out));
  Adder #(.width(16)) adder_1 (.a(PC_out), .b(bit_extender_2_out), .out(adder_1_out));  // open: cin, cout
  Multiplexer #(.width(16)) multiplexer_5 (
    .in0(adder_1_out), .in1(bit_extender_4_out), .out(multiplexer_5_out), .sel(comparator_1_eq));
  Comparator #(.width(4)) comparator_1 (.a(decoder_logic_1_opcode), .b(4'b1010), .eq(comparator_1_eq));  // open: gt, lt

  // Other names for the same wires on the sheet: inst_out[15:0] = IR_instOut; write_data[7:0] = REG_writeData
endmodule
