// Logisim project data_memory.circ as structural Verilog: 1 circuit, main circuit data_memory
module data_memory (
  input  [7:0] address,
  input  mem_write,
  input  mem_read,
  input  clk,
  input  [7:0] write_data,
  output [7:0] read_data
);

  RAM ram_1 (.addr(address), .we(mem_write), .oe(mem_read), .clk(clk), .din(write_data), .dout(read_data));
endmodule
