// Logisim project decoder_logic.circ as structural Verilog: 1 circuit, main circuit decoder_logic
module decoder_logic (
  input  [15:0] instruction,
  output [5:0] imm6,
  output [2:0] rs,
  output [2:0] rd,
  output [3:0] opcode
);


  assign imm6 = instruction[5:0];
  assign opcode = instruction[15:12];
  assign rd = instruction[11:9];
  assign rs = instruction[8:6];
endmodule
