// Logisim project instruction_memory.circ as structural Verilog: 1 circuit, main circuit instruction_memory
module instruction_memory (
  input  [7:0] address,
  output [15:0] instruction
);

  ROM #(.dataWidth(16)) rom_1 (.addr(address), .data(instruction));

  // Notes on the sheet:
  //   contents of rom_1 (hex, n*v repeats v):
  //   9205 9403 1640 1680 760a 640a eb00
endmodule
