// Logisim project instruction_register.circ as structural Verilog: 1 circuit, main circuit instruction_register
module instruction_register (
  input  [15:0] instruction_in,
  input  reset,
  input  ir_load,
  input  clk,
  output [15:0] instruction_out
);

  wire or_1_out;
  wire [15:0] multiplexer_1_out;

  Multiplexer #(.width(16)) multiplexer_1 (
    .in0(instruction_in), .in1({16{1'b0}}), .out(multiplexer_1_out), .sel(reset));
  or or_1 (or_1_out, reset, ir_load);
  Register #(.width(16)) REG_IR (.D(multiplexer_1_out), .en(or_1_out), .clk(clk), .Q(instruction_out));  // open: clr
endmodule
