// Logisim project program_counter.circ as structural Verilog: 1 circuit, main circuit program_counter
module program_counter (
  input  clk,
  input  [15:0] pc_next,
  input  reset,
  input  pc_load,
  input  pc_enable,
  output [15:0] pc_out
);

  wire [15:0] adder_1_out, multiplexer_1_out, multiplexer_2_out, multiplexer_3_out;

  Register #(.width(16)) REG_PC (.D(multiplexer_3_out), .clk(clk), .Q(pc_out));  // open: en, clr
  Adder #(.width(16)) adder_1 (.a(pc_out), .b(16'h1), .out(adder_1_out));  // open: cin, cout
  Multiplexer #(.width(16)) multiplexer_1 (.in0(pc_out), .in1(adder_1_out), .out(multiplexer_1_out), .sel(pc_enable));
  Multiplexer #(.width(16)) multiplexer_2 (
    .in0(multiplexer_1_out), .in1(pc_next), .out(multiplexer_2_out), .sel(pc_load));
  Multiplexer #(.width(16)) multiplexer_3 (
    .in0(multiplexer_2_out), .in1({16{1'b0}}), .out(multiplexer_3_out), .sel(reset));
endmodule
