// Logisim project reg_file.circ as structural Verilog: 1 circuit, main circuit reg_file
module reg_file (
  input  reg_write,
  input  [2:0] write_reg,
  input  [7:0] write_data,
  input  clk,
  input  reset,
  input  [2:0] read_reg1,
  input  [2:0] read_reg2,
  output [7:0] read_data1,
  output [7:0] read_data2
);

  wire and_1_out, and_2_out, and_3_out, and_4_out, and_5_out, and_6_out, and_7_out, comparator_1_eq,
       comparator_2_eq, comparator_3_eq, comparator_4_eq, comparator_5_eq, comparator_6_eq, comparator_7_eq;
  wire [7:0] register_1_q, register_2_q, register_3_q, register_4_q, register_5_q, register_6_q, register_7_q;

  Register register_1 (.D(write_data), .en(and_1_out), .clk(clk), .Q(register_1_q), .clr(reset));
  Register register_2 (.D(write_data), .en(and_2_out), .clk(clk), .Q(register_2_q), .clr(reset));
  Register register_3 (.D(write_data), .en(and_3_out), .clk(clk), .Q(register_3_q), .clr(reset));
  Register register_4 (.D(write_data), .en(and_4_out), .clk(clk), .Q(register_4_q), .clr(reset));
  Register register_5 (.D(write_data), .en(and_5_out), .clk(clk), .Q(register_5_q), .clr(reset));
  Register register_6 (.D(write_data), .en(and_6_out), .clk(clk), .Q(register_6_q), .clr(reset));
  Register register_7 (.D(write_data), .en(and_7_out), .clk(clk), .Q(register_7_q), .clr(reset));
  Comparator #(.width(3)) comparator_1 (.a(write_reg), .b(3'b001), .eq(comparator_1_eq));  // open: gt, lt
  Comparator #(.width(3)) comparator_2 (.a(write_reg), .b(3'b010), .eq(comparator_2_eq));  // open: gt, lt
  Comparator #(.width(3)) comparator_3 (.a(write_reg), .b(3'b011), .eq(comparator_3_eq));  // open: gt, lt
  Comparator #(.width(3)) comparator_4 (.a(write_reg), .b(3'b100), .eq(comparator_4_eq));  // open: gt, lt
  Comparator #(.width(3)) comparator_5 (.a(write_reg), .b(3'b101), .eq(comparator_5_eq));  // open: gt, lt
  Comparator #(.width(3)) comparator_6 (.a(write_reg), .b(3'b110), .eq(comparator_6_eq));  // open: gt, lt
  Comparator #(.width(3)) comparator_7 (.a(write_reg), .b(3'b111), .eq(comparator_7_eq));  // open: gt, lt
  and and_1 (and_1_out, comparator_1_eq, reg_write);
  Multiplexer #(.select(3), .width(8)) multiplexer_1 (
    .in0({8{1'b0}}), .in1(register_1_q), .in2(register_2_q), .in3(register_3_q), .in4(register_4_q),
    .in5(register_5_q), .in6(register_6_q), .in7(register_7_q), .out(read_data1), .sel(read_reg1));
  Multiplexer #(.select(3), .width(8)) multiplexer_2 (
    .in0({8{1'b0}}), .in1(register_1_q), .in2(register_2_q), .in3(register_3_q), .in4(register_4_q),
    .in5(register_5_q), .in6(register_6_q), .in7(register_7_q), .out(read_data2), .sel(read_reg2));
  and and_2 (and_2_out, comparator_2_eq, reg_write);
  and and_3 (and_3_out, comparator_3_eq, reg_write);
  and and_4 (and_4_out, comparator_4_eq, reg_write);
  and and_5 (and_5_out, comparator_5_eq, reg_write);
  and and_6 (and_6_out, comparator_6_eq, reg_write);
  and and_7 (and_7_out, comparator_7_eq, reg_write);
endmodule
